// Logisim project p0_课下01.circ as structural Verilog: 2 circuits, main circuit CRC
module CRC (
  input  [7:0] A,
  input  [3:0] B,
  output [10:0] C
);

  wire [2:0] mini_crc_1_r, mini_crc_2_r, mini_crc_3_r, mini_crc_4_r, mini_crc_5_r, mini_crc_6_r, mini_crc_7_r;

  mini_crc mini_crc_1 (.X(A[7:4]), .B(B), .R(mini_crc_1_r));
  mini_crc mini_crc_2 (.X({mini_crc_1_r, A[3]}), .B(B), .R(mini_crc_2_r));
  mini_crc mini_crc_3 (.X({mini_crc_2_r, A[2]}), .B(B), .R(mini_crc_3_r));
  mini_crc mini_crc_4 (.X({mini_crc_3_r, A[1]}), .B(B), .R(mini_crc_4_r));
  mini_crc mini_crc_5 (.X({mini_crc_4_r, A[0]}), .B(B), .R(mini_crc_5_r));
  mini_crc mini_crc_6 (.X({mini_crc_5_r, 1'b0}), .B(B), .R(mini_crc_6_r));
  mini_crc mini_crc_7 (.X({mini_crc_6_r, 1'b0}), .B(B), .R(mini_crc_7_r));
  mini_crc mini_crc_8 (.X({mini_crc_7_r, 1'b0}), .B(B), .R(C[2:0]));

  assign C[10:3] = A;
endmodule

module mini_crc (
  input  [3:0] X,
  input  [3:0] B,
  output [2:0] R
);

  wire and_1_out, and_2_out, and_3_out;

  and and_1 (and_1_out, X[3], B[2]);
  and and_2 (and_2_out, X[3], B[1]);
  and and_3 (and_3_out, X[3], B[0]);
  xor xor_1 (R[2], X[2], and_1_out);
  xor xor_2 (R[1], X[1], and_2_out);
  xor xor_3 (R[0], X[0], and_3_out);
endmodule
