// Logisim project p0_课下03.circ as structural Verilog: 1 circuit, main circuit navigation
module navigation (
  input  [1:0] dir,
  input  clk,
  input  reset,
  output arrive,
  output hit
);

  wire A0OUT, A_q, and_1_out, and_2_out, and_3_out, and_4_out, and_5_out, and_6_out, and_7_out, and_8_out,
       and_9_out, and_10_out, and_11_out, and_12_out, and_13_out, and_14_out, AOUT, C0OUT, COUT, D0OUT, DOUT,
       DOWN, E0OUT, EOUT, LEFT, not_1_out, not_2_out, or_2_out, or_3_out, or_6_out, or_9_out, or_10_out, PA,
       PC, PD, PE, RIGHT, UP;

  Decoder #(.select(2), .enable("false")) decoder_1 (.out0(UP), .out1(RIGHT), .out2(DOWN), .out3(LEFT), .sel(dir));
  or or_1 (PA, AOUT, A0OUT);
  and and_1 (and_1_out, PC, DOWN);
  or or_2 (or_2_out, and_1_out, arrive);
  not not_1 (not_1_out, UP);
  and and_2 (and_2_out, PD, UP);
  and and_3 (and_3_out, PE, RIGHT);
  Register #(.width(1)) A (.D(not_2_out), .en(1'b1), .Q(A_q), .clk(clk), .clr(reset));
  not not_2 (not_2_out, or_2_out);
  and and_4 (and_4_out, PA, not_1_out);
  or or_3 (or_3_out, and_2_out, and_3_out);
  or or_4 (PC, COUT, C0OUT);
  not not_3 (AOUT, A_q);
  Register #(.width(1)) A0 (.D(and_4_out), .en(1'b1), .Q(A0OUT), .clk(clk), .clr(reset));
  Register #(.width(1)) B (.D(or_3_out), .en(1'b1), .Q(arrive), .clk(clk), .clr(reset));
  or or_5 (PD, DOUT, D0OUT);
  and and_5 (and_5_out, PA, UP);
  and and_6 (and_6_out, PD, LEFT);
  and and_7 (and_7_out, PE, DOWN);
  or or_6 (or_6_out, and_5_out, and_6_out, and_7_out);
  Register #(.width(1)) C0 (.D(and_8_out), .en(1'b1), .Q(C0OUT), .clk(clk), .clr(reset));
  and and_8 (and_8_out, PC, LEFT);
  or or_7 (PE, EOUT, E0OUT);
  Register #(.width(1)) C (.D(or_6_out), .en(1'b1), .Q(COUT), .clk(clk), .clr(reset));
  or or_8 (hit, A0OUT, C0OUT, D0OUT, E0OUT);
  and and_9 (and_9_out, PD, RIGHT);
  and and_10 (and_10_out, PD, DOWN);
  Register #(.width(1)) D (.D(and_11_out), .en(1'b1), .Q(DOUT), .clk(clk), .clr(reset));
  and and_11 (and_11_out, PC, RIGHT);
  Register #(.width(1)) D0 (.D(or_9_out), .en(1'b1), .Q(D0OUT), .clk(clk), .clr(reset));
  or or_9 (or_9_out, and_9_out, and_10_out);
  and and_12 (and_12_out, PE, LEFT);
  and and_13 (and_13_out, PE, UP);
  and and_14 (and_14_out, PC, UP);
  Register #(.width(1)) E (.D(and_14_out), .en(1'b1), .Q(EOUT), .clk(clk), .clr(reset));
  or or_10 (or_10_out, and_12_out, and_13_out);
  Register #(.width(1)) E0 (.D(or_10_out), .en(1'b1), .Q(E0OUT), .clk(clk), .clr(reset));

  // Other names for the same wires on the sheet: BOUT = arrive
endmodule
