// Logisim project p0_课下04.circ as structural Verilog: 1 circuit, main circuit fsm
module fsm (
  input  [1:0] In,
  input  CLR,
  output Z
);

  wire AC, and_1_out, and_2_out, and_3_out, B, CLK, decoder_1_out0, decoder_1_out2, not_1_out, not_2_out, O,
       or_1_out, or_3_out, S0OUT, S1OUT, S2OUT;

  Clock clock_1 (.out(CLK));
  Decoder #(.select(2), .enable("false")) decoder_1 (
    .out0(decoder_1_out0), .out1(B), .out2(decoder_1_out2), .out3(O), .sel(In));
  or or_1 (or_1_out, S2OUT, S0OUT);
  or or_2 (AC, decoder_1_out0, decoder_1_out2);
  and and_1 (and_1_out, or_1_out, AC);
  not not_1 (not_1_out, CLR);
  or or_3 (or_3_out, and_1_out, O, CLR);
  and and_2 (and_2_out, not_1_out, S1OUT, AC);
  Register #(.width(1)) S0 (.D(or_3_out), .en(1'b1), .Q(S0OUT), .clk(CLK), .clr(1'b0));
  Register #(.width(1)) S2 (.D(and_2_out), .en(1'b1), .Q(S2OUT), .clk(CLK), .clr(1'b0));
  not not_2 (not_2_out, CLR);
  and and_3 (and_3_out, not_2_out, B);
  and and_4 (Z, S2OUT, AC);
  Register #(.width(1)) S1 (.D(and_3_out), .en(1'b1), .Q(S1OUT), .clk(CLK), .clr(1'b0));
endmodule
