// Logisim project p0_课下附加01.circ as structural Verilog: 1 circuit, main circuit ftoi
module ftoi (
  input  [15:0] float,
  output [31:0] \int 
);

  wire comparator_1_lt, comparator_2_lt, comparator_3_eq, or_1_out;
  wire [4:0] LSHIFT, RSHIFT;
  wire [31:0] L, M, multiplexer_1_out, multiplexer_2_out, negator_1_out, R;

  Subtractor #(.width(5)) subtractor_1 (.a(float[14:10]), .b(5'b11001), .out(LSHIFT), .bin(1'b0));  // open: bout
  Subtractor #(.width(5)) subtractor_2 (.a(5'b11001), .b(float[14:10]), .out(RSHIFT), .bin(1'b0));  // open: bout
  Comparator #(.width(5), .mode("unsigned")) comparator_1 (
    .a(float[14:10]), .b(5'b11001), .lt(comparator_1_lt));  // open: gt, eq
  Multiplexer #(.width(32), .enable("false")) multiplexer_1 (
    .in0(L), .in1(R), .out(multiplexer_1_out), .sel(comparator_1_lt));
  assign M = {{21{1'b0}}, {1'b1, float[9:0]}};  // Bit_Extender bit_extender_1
  Shifter #(.width(32)) shifter_1 (.in(M), .\dist (LSHIFT), .out(L));
  Shifter #(.width(32), .shift("lr")) shifter_2 (.in(M), .\dist (RSHIFT), .out(R));
  Negator #(.width(32)) negator_1 (.in(multiplexer_1_out), .out(negator_1_out));
  Comparator #(.width(5), .mode("unsigned")) comparator_2 (
    .a(float[14:10]), .b(5'b01111), .lt(comparator_2_lt));  // open: gt, eq
  Comparator #(.width(5), .mode("unsigned")) comparator_3 (
    .a(float[14:10]), .b({5{1'b1}}), .eq(comparator_3_eq));  // open: gt, lt
  Multiplexer #(.width(32), .enable("false")) multiplexer_2 (
    .in0(multiplexer_1_out), .in1(negator_1_out), .out(multiplexer_2_out), .sel(float[15]));
  or or_1 (or_1_out, comparator_2_lt, comparator_3_eq);
  Multiplexer #(.width(32), .enable("false")) multiplexer_3 (
    .in0(multiplexer_2_out), .in1({32{1'b0}}), .out(\int ), .sel(or_1_out));

  // Other names for the same wires on the sheet: F[9:0] = float[9:0]; E[4:0] = float[14:10]; SIGN = float[15]
endmodule
