// Logisim project pre_01.circ as structural Verilog: 1 circuit, main circuit main
module main (
  input  [7:0] in_1,
  output [5:0] out_2
);

  wire _0001, and_1_out, and_2_out, and_3_out, and_4_out, and_5_out, comparator_1_eq, comparator_1_gt,
       comparator_1_lt, comparator_2_gt, comparator_2_lt, not_1_out, or_1_out, or_2_out;
  wire [3:0] adder_1_out, multiplexer_5_out, subtractor_1_out, subtractor_2_out, subtractor_3_out;

  Multiplexer #(.width(2), .enable("false")) multiplexer_1 (
    .in1(2'b00), .out(out_2[5:4]), .sel(comparator_1_eq));  // open: in0
  Multiplexer #(.width(2), .enable("false")) multiplexer_2 (
    .in1(2'b01), .out(out_2[5:4]), .sel(or_1_out));  // open: in0
  Multiplexer #(.width(2), .enable("false")) multiplexer_3 (
    .in1(2'b10), .out(out_2[5:4]), .sel(or_2_out));  // open: in0
  Multiplexer #(.width(2), .enable("false")) multiplexer_4 (
    .in1(2'b11), .out(out_2[5:4]), .sel(and_4_out));  // open: in0
  Subtractor #(.width(4)) subtractor_1 (.a(in_1[3:0]), .b(in_1[7:4]), .out(subtractor_1_out));  // open: bin, bout
  Subtractor #(.width(4)) subtractor_2 (.a(in_1[7:4]), .b(in_1[3:0]), .out(subtractor_2_out));  // open: bin, bout
  Comparator #(.width(4), .mode("unsigned")) comparator_1 (
    .a(in_1[3:0]), .b(in_1[7:4]), .gt(comparator_1_gt), .eq(comparator_1_eq), .lt(comparator_1_lt));
  Subtractor #(.width(4)) subtractor_3 (.a(4'b1111), .b(multiplexer_5_out), .out(subtractor_3_out));  // open: bin, bout
  Multiplexer #(.width(4), .enable("false")) multiplexer_5 (
    .in0(subtractor_1_out), .in1(subtractor_2_out), .out(multiplexer_5_out), .sel(comparator_1_lt));
  not not_1 (not_1_out, comparator_1_eq);
  Adder #(.width(4)) adder_1 (.a(4'b0001), .b(subtractor_3_out), .out(adder_1_out));  // open: cin, cout
  Comparator #(.width(4), .mode("unsigned")) comparator_2 (
    .a(multiplexer_5_out), .b(4'b1000), .gt(comparator_2_gt), .eq(_0001), .lt(comparator_2_lt));
  and and_1 (and_1_out, comparator_2_lt, comparator_1_gt);
  and and_2 (and_2_out, comparator_2_lt, comparator_1_lt);
  and and_3 (and_3_out, comparator_2_gt, comparator_1_gt);
  and and_4 (and_4_out, not_1_out, _0001);
  Multiplexer #(.width(4), .enable("false")) multiplexer_6 (
    .in0(multiplexer_5_out), .in1(adder_1_out), .out(out_2[3:0]), .sel(comparator_2_gt));
  and and_5 (and_5_out, comparator_2_gt, comparator_1_lt);
  or or_1 (or_1_out, and_5_out, and_1_out);
  or or_2 (or_2_out, and_2_out, and_3_out);

  // Notes on the sheet:
  //   00
  //   01
  //   10
  //   11
endmodule
